// Digital circuit 16-bit_presettable_counter.dig as structural Verilog
module _16_bit_presettable_counter (
  input  en,
  input  c,
  input  dir,
  input  [7:0] lo_in,
  input  lo_ld,
  input  [7:0] hi_in,
  input  hi_ld,
  input  clr,
  output ovf,
  output [7:0] lo,
  output [7:0] hi
);

  wire LOW_ovf;

  CounterPreset #(.Bits(8)) u_HI (
    .en(en), .C(LOW_ovf), .dir(dir), .in(hi_in), .ld(hi_ld), .clr(clr), .out(hi), .ovf(ovf));
  CounterPreset #(.Bits(8)) LOW (.en(en), .C(c), .dir(dir), .in(lo_in), .ld(lo_ld), .clr(clr), .out(lo), .ovf(LOW_ovf));
  // Pins of 1 and 8 bits meet at lo_in
  // Pins of 1 and 8 bits meet at hi_in
endmodule
