// Digital circuit alu.dig as structural Verilog
module alu (
  input  [7:0] B,
  input  [3:0] flags,
  input  [2:0] op,
  input  [7:0] A,
  output [7:0] s,
  output [3:0] flag_mask,
  output [3:0] flag_value
);

  wire and_1_out, and_2_out, and_3_out, and_4_out, not_1_out, not_2_out, not_3_out, not_4_out, not_5_out,
       not_6_out, P_add_v, P_c_add, P_c_sub, P_sub_v, P_z;
  wire [7:0] ADD, AND, not_7_out, OR, SHR, SUB;

  not not_1 (not_1_out, s[7]);
  not not_2 (not_2_out, A[7]);
  not not_3 (not_3_out, B[7]);
  not not_4 (not_4_out, s[7]);
  not not_5 (not_5_out, B[7]);
  not not_6 (not_6_out, A[7]);
  and and_1 (and_1_out, A[7], not_1_out, B[7]);
  and and_2 (and_2_out, not_2_out, s[7], not_3_out);
  and and_3 (and_3_out, A[7], not_4_out, not_5_out);
  and and_4 (and_4_out, not_6_out, s[7], B[7]);
  or or_1 (P_sub_v, and_3_out, and_4_out);
  or or_2 (P_add_v, and_1_out, and_2_out);
  assign not_7_out = ~B;  // Not not_7, 8 bits wide
  BarrelShifter #(.Bits(8), .direction("right")) barrelshifter_1 (.in(B), .shift(4'b0001), .out(SHR));
  nor nor_1 (P_z, s[0], s[1], s[2], s[3], s[4], s[5], s[6], s[7]);
  Add #(.Bits(8)) add_1 (.a(A), .b(B), .c_i(1'b0), .s(ADD), .c_o(P_c_add));
  Add #(.Bits(8)) add_2 (.a(A), .b(not_7_out), .c_i(1'b1), .s(SUB), .c_o(P_c_sub));
  assign AND = B & A;  // And and_5, 8 bits wide
  assign OR = B | A;  // Or or_3, 8 bits wide
  Multiplexer #(.Selector_Bits(3), .Bits(8)) multiplexer_1 (
    .sel(op), .in_0(A), .in_1(B), .in_2(ADD), .in_3(SUB), .in_4(AND), .in_5(OR), .in_6(SHR),
    .in_7({8{1'b1}}), .out(s));
  Multiplexer #(.Selector_Bits(3), .Bits(4)) multiplexer_2 (
    .sel(op), .in_0(4'b0110), .in_1(4'b0110), .in_2(4'b1111), .in_3(4'b1111), .in_4(4'b0110), .in_5(4'b0110),
    .in_6(4'b0110), .in_7(4'b0000), .out(flag_mask));
  Multiplexer #(.Selector_Bits(3), .Bits(4)) multiplexer_3 (
    .sel(op), .in_0({flags[3], P_z, s[7], flags[0]}), .in_1({flags[3], P_z, s[7], flags[0]}),
    .in_2({P_add_v, P_z, s[7], P_c_add}), .in_3({P_sub_v, P_z, s[7], P_c_sub}),
    .in_4({flags[3], P_z, s[7], flags[0]}), .in_5({flags[3], P_z, s[7], flags[0]}),
    .in_6({flags[3], P_z, s[7], flags[0]}), .in_7(flags), .out(flag_value));

  // Other names for the same wires on the sheet: C = flags[0]; N = flags[1]; Z = flags[2]; V = flags[3]; P_n = s[7]
endmodule
