// Digital circuit bus_transceiver.dig as structural Verilog
module bus_transceiver (
  input  dir,
  input  oe,
  input  [7:0] a,
  input  [7:0] b
);

  wire and_1_out, and_2_out;
  wire [7:0] undriven, undriven_2;

  and and_1 (and_1_out, dir, ~oe);  // And
  Driver #(.invertDriverOutput("true"), .Bits(8)) driver_1 (.in(a), .en(and_1_out));  // open: out
  Driver #(.invertDriverOutput("true"), .Bits(8)) driver_2 (.in(undriven), .en(and_1_out));  // open: out
  Driver #(.invertDriverOutput("true"), .Bits(8)) driver_3 (.in(undriven_2), .en(and_2_out));  // open: out
  and and_2 (and_2_out, ~oe, ~dir);  // And
  Driver #(.invertDriverOutput("true"), .Bits(8)) driver_4 (.in(b), .en(and_2_out));  // open: out
endmodule
