// Digital circuit computer.dig as structural Verilog
module computer (
  input  clk
);

  wire demultiplexer_3_out_2, demultiplexer_3_out_3, demultiplexer_4_out_2, demultiplexer_4_out_3, IO_OE,
       IO_WE, KEYBOARD_OE, MEM_OE, MEM_WE, RAM_OE, RAM_WE, ROM_OE, ROM_WE, TERMINAL_WE;
  wire [1:0] MEM_SEL;
  wire [7:0] DBUS_I, DBUS_O;
  wire [13:0] MEM_ADDR;
  wire [15:8] keyboard_1_d;

  Demultiplexer #(.Selector_Bits(4)) demultiplexer_1 (
    .sel(MEM_ADDR[3:0]), .in(IO_WE), .out_0(TERMINAL_WE));  // open: out_1, out_2, out_3, out_4, out_5, out_6, out_7, out_8, out_9, out_10, out_11, out_12, out_13, out_14, out_15
  Demultiplexer #(.Selector_Bits(4)) demultiplexer_2 (
    .sel(MEM_ADDR[3:0]), .in(IO_OE), .out_0(KEYBOARD_OE));  // open: out_1, out_2, out_3, out_4, out_5, out_6, out_7, out_8, out_9, out_10, out_11, out_12, out_13, out_14, out_15
  main main_1 (.C(clk), .DBUS(DBUS_I), .ABUS({MEM_SEL, MEM_ADDR}), .DBUS_O(DBUS_O), .MEM_OE(MEM_OE), .MEM_WE(MEM_WE));
  Keyboard keyboard_1 (.C(clk), .en(KEYBOARD_OE), .D({keyboard_1_d, DBUS_I}));  // open: av
  ROM #(.AddrBits(14), .Bits(8)) rom_1 (.A(MEM_ADDR), .sel(ROM_OE), .D(DBUS_I));
  RAMDualPort #(.AddrBits(14), .Bits(8)) ramdualport_1 (
    .A(MEM_ADDR), .Din(DBUS_O), .str(RAM_WE), .C(clk), .ld(RAM_OE), .D(DBUS_I));
  Terminal terminal_1 (.D(DBUS_O), .C(clk), .en(TERMINAL_WE));
  or or_1 (RAM_WE, demultiplexer_3_out_2, demultiplexer_3_out_3);
  or or_2 (RAM_OE, demultiplexer_4_out_2, demultiplexer_4_out_3);
  Demultiplexer #(.Selector_Bits(2)) demultiplexer_3 (
    .sel(MEM_SEL), .in(MEM_WE), .out_0(ROM_WE), .out_1(IO_WE), .out_2(demultiplexer_3_out_2),
    .out_3(demultiplexer_3_out_3));
  Demultiplexer #(.Selector_Bits(2)) demultiplexer_4 (
    .sel(MEM_SEL), .in(MEM_OE), .out_0(ROM_OE), .out_1(IO_OE), .out_2(demultiplexer_4_out_2),
    .out_3(demultiplexer_4_out_3));

  // Notes on the sheet:
  //   clk: Hz: 2147483647
  //   contents of rom_1 (hex, n*v repeats v):
  //   48,24,1,48,0,2,6e,0,73,44,48,0,4,1c,b,68,11,8b,40,0,9,50,1,1,6c
  //   ,2,6e,4,a,50,1,2,6e,e6,6e,fe,4c,6f,72,65,6d,20,69,70,73,75,6d
  //   ,20,64,6f,6c,6f,72,20,73,69,74,20,61,6d,65,74,2c,20,63,6f,6e,73
  //   ,65,63,74,65,74,75,72,20,61,64,69,70,69,73,63,69,6e,67,20,65,6c
  //   ,69,74,2c,20,73,65,64,20,64,6f,20,65,69,75,73,6d,6f,64,20,74,65
  //   ,6d,70,6f,72,20,69,6e,63,69,64,69,64,75,6e,74,20,75,74,20,6c,61
  //   ,62,6f,72,65,20,65,74,20,64,6f,6c,6f,72,65,20,6d,61,67,6e,61,20
  //   ,61,6c,69,71,75,61,2e,20,55,74,20,65,6e,69,6d,20,61,64,20,6d,69
  //   ,6e,69,6d,20,76,65,6e,69,61,6d,2c,20,71,75,69,73,20,6e,6f,73,74
  //   ,72,75,64,20,65,78,65,72,63,69,74,61,74,69,6f,6e,20,75,6c,6c,61
  //   ,6d,63,6f,20,6c,61,62,6f,72,69,73,20,6e,69,73,69,20,75,74,20,61
  //   ,6c,69,71,75,69,70,20,65,78,20,65,61,20,63,6f,6d,6d,6f,64,6f,20
  //   ,63,6f,6e,73,65,71,75,61,74,2e,20,44,75,69,73,20,61,75,74,65,20
  //   ,69,72,75,72,65,20,64,6f,6c,6f,72,20,69,6e,20,72,65,70,72,65,68
  //   ,65,6e,64,65,72,69,74,20,69,6e,20,76,6f,6c,75,70,74,61,74,65,20
  //   ,76,65,6c,69,74,20,65,73,73,65,20,63,69,6c,6c,75,6d,20,64,6f,6c
  //   ,6f,72,65,20,65,75,20,66,75,67,69,61,74,20,6e,75,6c,6c,61,20,70
  //   ,61,72,69,61,74,75,72,2e,20,45,78,63,65,70,74,65,75,72,20,73,69
  //   ,6e,74,20,6f,63,63,61,65,63,61,74,20,63,75,70,69,64,61,74,61,74
  //   ,20,6e,6f,6e,20,70,72,6f,69,64,65,6e,74,2c,20,73,75,6e,74,20,69
  //   ,6e,20,63,75,6c,70,61,20,71,75,69,20,6f,66,66,69,63,69,61,20,64
  //   ,65,73,65,72,75,6e,74,20,6d,6f,6c,6c,69,74,20,61,6e,69,6d,20,69
  //   ,64,20,65,73,74,20,6c,61,62,6f,72,75,6d,2e
endmodule
