// Digital circuit condition_unit.dig as structural Verilog
module condition_unit (
  input  [2:0] cond,
  input  [3:0] flags,
  output nout
);

  wire multiplexer_1_out, not_1_out, not_2_out, not_3_out, xor_1_out;

  xor xor_1 (xor_1_out, flags[1], flags[3]);
  not not_1 (not_1_out, flags[2]);
  not not_2 (not_2_out, xor_1_out);
  not not_3 (not_3_out, flags[0]);
  Multiplexer #(.Selector_Bits(3)) multiplexer_1 (
    .sel(cond), .in_0(flags[2]), .in_1(not_1_out), .in_2(xor_1_out), .in_3(not_2_out), .in_4(flags[0]),
    .in_5(not_3_out), .in_6(1'b1), .in_7(1'b1), .out(multiplexer_1_out));
  not not_4 (nout, multiplexer_1_out);

  // Other names for the same wires on the sheet: C = flags[0]; N = flags[1]; Z = flags[2]; V = flags[3]
endmodule
