// Digital circuit instruction_decoder.dig as structural Verilog
module instruction_decoder (
  input  [7:0] b0,
  input  [7:0] b1,
  input  [7:0] b2,
  output [1:0] ll,
  output [2:0] ooo,
  output [2:0] vvv,
  output [7:0] imm8,
  output [2:0] rs0,
  output [2:0] rs1,
  output [15:0] imm16
);

  // Pins of 2 and 3 bits meet at b0[2:0]
  // Pins of 2 and 3 bits meet at b0[5:3]
  // Pins of 1 and 3 bits meet at b1[4:2]
  // Pins of 1 and 3 bits meet at b1[7:5]

  assign imm8 = b1;
  assign imm16 = {b1, b2};
  assign ll = b0[7:6];
  assign ooo = b0[5:3];
  assign rs0 = b1[4:2];
  assign rs1 = b1[7:5];
  assign vvv = b0[2:0];
endmodule
