// Digital circuit main_inside.dig as structural Verilog
module main_inside (
  input  C,
  output [15:0] ABUS
);

  wire A_RD_DB, A_WR_ALU, A_WR_DB, ACC_WR_DB, and_1_out, and_2_out, B_RD_DB, B_WR_ALU, B_WR_DB, C_RD_DB,
       C_WR_ALU, C_WR_DB, condition_unit_1_out, D_RD_DB, D_WR_ALU, D_WR_DB, demultiplexer_3_out_2,
       demultiplexer_3_out_3, demultiplexer_4_out_2, demultiplexer_4_out_3, IMM16_WR_AB, IN_WR_DB, IO_OE,
       IO_WE, IR0_RD, IR1_RD, IR2_RD, KEYBOARD_OE, MEM_OE, MEM_WE, microcode_1_upc_clr,
       microcode_1_upc_cond_clr, not_1_out, ooo, or_1_out, PC1_Hi_WRDB, PC1_Lo_WRDB, PC_H_WE, PC_INC,
       PC_L_WE, PC_ovf, PC_WR_AB, RAM_OE, RAM_WE, ROM_OE, ROM_WE, RS0_PAIR_WR_A, RS0_PAIR_WR_B,
       RS0_PAIR_WR_C, RS0_PAIR_WR_D, RS0_RD_DB, RS0_WR_DB, RS1_PAIR_WR_A, RS1_PAIR_WR_B, RS1_PAIR_WR_C,
       RS1_PAIR_WR_D, RS1_RD_DB, RS1_WR_DB, RS_PAIR_WR_AB, SP_DEC, SP_H_RD_DB, SP_H_WR_DB, SP_INC,
       SP_L_RD_DB, SP_L_WR_DB, SP_ovf, SP_WR_AB, STORE_ACC, STORE_C, STORE_FLAG, STORE_N, STORE_V, STORE_Z,
       TERMINAL_WE, VVV_RD_DB, VVV_WR_DB;
  wire [1:0] ll;
  wire [2:0] AB_WR_DEV, DB_RD_DEV, DB_WR_DEV, PC_SRC, rs0, rs1, vvv;
  wire [3:0] alu_1_p4, FLAG_Data, microcode_1_upc;
  wire [7:0] A_q, ACC_Data, alu_1_p1, B_q, C_q, D_q, DBUS, driver_1_out, driver_22_out, imm8,
       instruction_decoder_1_p4, instruction_decoder_1_p6, IR0_Data, multiplexer_1_out, multiplexer_2_out,
       SP_hi, SP_lo;
  wire [11:0] microcode_1_addr;
  wire [15:0] add_1_s, add_2_s, bitextender_1_out, driver_12_out, imm16, PC_Data;
  wire [15:8] keyboard_1_d;

  Demultiplexer #(.Selector_Bits(4)) demultiplexer_1 (
    .sel(ABUS[3:0]), .in(IO_WE), .out_0(TERMINAL_WE));  // open: out_1, out_2, out_3, out_4, out_5, out_6, out_7, out_8, out_9, out_10, out_11, out_12, out_13, out_14, out_15
  condition_unit condition_unit_1 (.cond(vvv), .flags(FLAG_Data), .out(condition_unit_1_out));
  and and_1 (and_1_out, microcode_1_upc_cond_clr, condition_unit_1_out);
  Decoder #(.Selector_Bits(3)) decoder_1 (
    .sel(rs0), .out_1(RS0_PAIR_WR_A), .out_2(RS0_PAIR_WR_B), .out_3(RS0_PAIR_WR_C), .out_4(RS0_PAIR_WR_D));  // open: out_0, out_5, out_6, out_7
  Decoder #(.Selector_Bits(3)) decoder_2 (
    .sel(DB_RD_DEV), .out_1(VVV_RD_DB), .out_2(RS0_RD_DB), .out_3(RS1_RD_DB));  // open: out_0, out_4, out_5, out_6, out_7
  LED led_1 (.in(microcode_1_upc_clr));
  microcode microcode_1 (
    .d0(IR0_Data), .c(C), .uPC_clr_2(and_1_out), .uPC_CLR(microcode_1_upc_clr), .PC_INC(PC_INC),
    .PCL_WE(PC_L_WE), .PCH_WE(PC_H_WE), .IR0_RD(IR0_RD), .IR1_RD(IR1_RD), .IR2_RD(IR2_RD), .SP_INC(SP_INC),
    .SP_DEC(SP_DEC), .DB_RD_DEV(DB_RD_DEV), .DB_WR_DEV(DB_WR_DEV), .AB_WR_DEV(AB_WR_DEV),
    .STORE_FLAG(STORE_FLAG), .STORE_ACC(STORE_ACC), .MEM_WE(MEM_WE), .MEM_OE(MEM_OE), .PC_SRC(PC_SRC),
    .uPC_Cond_CLR(microcode_1_upc_cond_clr), .uPC(microcode_1_upc), .ADDR(microcode_1_addr),
    .STORE_N(STORE_N), .STORE_V(STORE_V), .STORE_C(STORE_C), .STORE_Z(STORE_Z));
  BitExtender bitextender_1 (.in(imm8), .out(bitextender_1_out));
  Decoder #(.Selector_Bits(3)) decoder_3 (
    .sel(vvv), .out_1(A_WR_ALU), .out_2(B_WR_ALU), .out_3(C_WR_ALU), .out_4(D_WR_ALU));  // open: out_0, out_5, out_6, out_7
  Decoder #(.Selector_Bits(3)) decoder_4 (
    .sel(rs1), .out_1(RS1_PAIR_WR_A), .out_2(RS1_PAIR_WR_B), .out_3(RS1_PAIR_WR_C), .out_4(RS1_PAIR_WR_D));  // open: out_0, out_5, out_6, out_7
  Demultiplexer #(.Selector_Bits(4)) demultiplexer_2 (
    .sel(ABUS[3:0]), .in(IO_OE), .out_0(KEYBOARD_OE));  // open: out_1, out_2, out_3, out_4, out_5, out_6, out_7, out_8, out_9, out_10, out_11, out_12, out_13, out_14, out_15
  or or_1 (or_1_out, SP_DEC, SP_INC);
  Add #(.Bits(16)) add_1 (.a(PC_Data), .b(bitextender_1_out), .c_i(1'b0), .s(add_1_s));  // open: c_o
  Add #(.Bits(16)) add_2 (.a(PC_Data), .b(16'h1), .c_i(1'b0), .s(add_2_s));  // open: c_o
  Multiplexer #(.Selector_Bits(3), .Bits(8)) multiplexer_1 (
    .sel(PC_SRC), .in_0(driver_1_out), .in_1(add_1_s[7:0]), .in_2(add_1_s[15:8]), .in_3(imm16[7:0]),
    .in_4(imm16[15:8]), .in_5({8{1'b0}}), .in_6({8{1'b0}}), .in_7({8{1'b0}}), .out(multiplexer_1_out));
  write_dbus_signals write_dbus_signals_1 (
    .vvv(vvv), .rs0(rs0), .rs1(rs1), .R_vvv(VVV_RD_DB), .R_rs0(RS0_RD_DB), .R_rs1(RS1_RD_DB), .A(A_RD_DB),
    .B(B_RD_DB), .C(C_RD_DB), .D(D_RD_DB), .SP_Hi(SP_H_RD_DB), .SP_Lo(SP_L_RD_DB));
  write_dbus_signals write_dbus_signals_2 (
    .vvv(vvv), .rs0(rs0), .rs1(rs1), .R_vvv(VVV_WR_DB), .R_rs0(RS0_WR_DB), .R_rs1(RS1_WR_DB), .A(A_WR_DB),
    .B(B_WR_DB), .C(C_WR_DB), .D(D_WR_DB), .SP_Hi(SP_H_WR_DB), .SP_Lo(SP_L_WR_DB));
  Decoder #(.Selector_Bits(3)) decoder_5 (
    .sel(DB_WR_DEV), .out_1(VVV_WR_DB), .out_2(RS0_WR_DB), .out_3(RS1_WR_DB), .out_4(ACC_WR_DB),
    .out_5(PC1_Lo_WRDB), .out_6(PC1_Hi_WRDB), .out_7(IN_WR_DB));  // open: out_0
  ROM #(.AddrBits(14), .Bits(8)) rom_1 (.A(ABUS[13:0]), .sel(ROM_OE), .D(DBUS));
  Keyboard keyboard_1 (.C(C), .en(KEYBOARD_OE), .D({keyboard_1_d, DBUS}));  // open: av
  _16_bit_presettable_counter PC (
    .en(PC_INC), .c(C), .dir(1'b0), .lo_in(multiplexer_1_out), .lo_ld(PC_L_WE), .hi_in(multiplexer_1_out),
    .hi_ld(PC_H_WE), .clr(1'b0), .ovf(PC_ovf), .lo(PC_Data[7:0]), .hi(PC_Data[15:8]));
  LED led_2 (.in(PC_ovf));
  assign driver_1_out = PC1_Lo_WRDB ? add_2_s[7:0] : 8'bz;  // Driver driver_1
  assign driver_1_out = PC1_Hi_WRDB ? add_2_s[15:8] : 8'bz;  // Driver driver_2
  _16_bit_presettable_counter SP (
    .en(or_1_out), .c(C), .dir(SP_DEC), .lo_in(driver_1_out), .lo_ld(SP_L_RD_DB), .hi_in(driver_1_out),
    .hi_ld(SP_H_RD_DB), .clr(1'b0), .ovf(SP_ovf), .lo(SP_lo), .hi(SP_hi));
  // Probe on SP_lo
  // Probe on SP_hi
  // Probe on microcode_1_upc
  // Probe on microcode_1_addr
  assign ABUS = PC_WR_AB ? PC_Data : 16'bz;  // Driver driver_3
  LED led_3 (.in(SP_ovf));
  assign ABUS = SP_WR_AB ? {SP_hi, SP_lo} : 16'bz;  // Driver driver_4
  assign driver_1_out = SP_L_WR_DB ? SP_lo : 8'bz;  // Driver driver_5
  assign driver_1_out = SP_H_WR_DB ? SP_hi : 8'bz;  // Driver driver_6
  RAMDualPort #(.AddrBits(14), .Bits(8)) ramdualport_1 (
    .A(ABUS[13:0]), .Din(DBUS), .str(RAM_WE), .C(C), .ld(RAM_OE), .D(DBUS));
  Decoder #(.Selector_Bits(3)) decoder_6 (
    .sel(AB_WR_DEV), .out_1(PC_WR_AB), .out_2(SP_WR_AB), .out_3(RS_PAIR_WR_AB), .out_4(IMM16_WR_AB));  // open: out_0, out_5, out_6, out_7
  bus_transceiver bus_transceiver_1 (.dir(not_1_out), .oe(1'b0), .a(driver_1_out), .b(DBUS));
  not not_1 (not_1_out, IN_WR_DB);
  Terminal terminal_1 (.D(DBUS), .C(C), .en(TERMINAL_WE));
  assign ABUS = IMM16_WR_AB ? imm16 : 16'bz;  // Driver driver_7
  assign ABUS = RS_PAIR_WR_AB ? driver_12_out : 16'bz;  // Driver driver_8
  assign driver_1_out = ACC_WR_DB ? ACC_Data : 8'bz;  // Driver driver_9
  or or_2 (RAM_WE, demultiplexer_3_out_2, demultiplexer_3_out_3);
  or or_3 (RAM_OE, demultiplexer_4_out_2, demultiplexer_4_out_3);
  // Probe on ACC_Data
  Register #(.Bits(8)) A (.D(driver_1_out), .C(C), .en(A_RD_DB), .Q(A_q));
  assign driver_1_out = A_WR_DB ? A_q : 8'bz;  // Driver driver_10
  assign driver_12_out[15:8] = RS0_PAIR_WR_A ? A_q : 8'bz;  // Driver driver_11
  assign driver_12_out[7:0] = RS1_PAIR_WR_A ? A_q : 8'bz;  // Driver driver_12
  Register #(.Bits(8)) B (.D(driver_1_out), .C(C), .en(B_RD_DB), .Q(B_q));
  assign driver_1_out = B_WR_DB ? B_q : 8'bz;  // Driver driver_13
  assign driver_12_out[15:8] = RS0_PAIR_WR_B ? B_q : 8'bz;  // Driver driver_14
  assign driver_12_out[7:0] = RS1_PAIR_WR_B ? B_q : 8'bz;  // Driver driver_15
  Register #(.Bits(8)) u_C (.D(driver_1_out), .C(C), .en(C_RD_DB), .Q(C_q));
  assign driver_1_out = C_WR_DB ? C_q : 8'bz;  // Driver driver_16
  assign driver_12_out[15:8] = RS0_PAIR_WR_C ? C_q : 8'bz;  // Driver driver_17
  assign driver_12_out[7:0] = RS1_PAIR_WR_C ? C_q : 8'bz;  // Driver driver_18
  Register #(.Bits(8)) D (.D(driver_1_out), .C(C), .en(D_RD_DB), .Q(D_q));
  assign driver_1_out = D_WR_DB ? D_q : 8'bz;  // Driver driver_19
  assign driver_12_out[15:8] = RS0_PAIR_WR_D ? D_q : 8'bz;  // Driver driver_20
  assign driver_12_out[7:0] = RS1_PAIR_WR_D ? D_q : 8'bz;  // Driver driver_21
  Demultiplexer #(.Selector_Bits(2)) demultiplexer_3 (
    .sel(ABUS[15:14]), .in(MEM_WE), .out_0(ROM_WE), .out_1(IO_WE), .out_2(demultiplexer_3_out_2),
    .out_3(demultiplexer_3_out_3));
  Demultiplexer #(.Selector_Bits(2)) demultiplexer_4 (
    .sel(ABUS[15:14]), .in(MEM_OE), .out_0(ROM_OE), .out_1(IO_OE), .out_2(demultiplexer_4_out_2),
    .out_3(demultiplexer_4_out_3));
  Register #(.Bits(8)) ACC (.D(alu_1_p1), .C(C), .en(STORE_ACC), .Q(ACC_Data));
  // Probe on A_q
  // Probe on B_q
  // Probe on C_q
  // Probe on D_q
  Multiplexer #(.Bits(8)) multiplexer_2 (.sel(and_2_out), .in_0(driver_22_out), .in_1(imm8), .out(multiplexer_2_out));
  assign driver_22_out = A_WR_ALU ? A_q : 8'bz;  // Driver driver_22
  assign driver_22_out = B_WR_ALU ? B_q : 8'bz;  // Driver driver_23
  assign driver_22_out = C_WR_ALU ? C_q : 8'bz;  // Driver driver_24
  assign driver_22_out = D_WR_ALU ? D_q : 8'bz;  // Driver driver_25
  // alu alu_1: pin names not known; wires that end beside it: alu_1_p1, multiplexer_2_out, FLAG_Data, alu_1_p4, ooo, ACC_Data
  and and_2 (and_2_out, ll[0], ~ll[1]);  // And
  Register #(.Bits(8)) IR0 (.D(driver_1_out), .C(C), .en(IR0_RD), .Q(IR0_Data));
  // Probe on instruction_decoder_1_p4
  // Probe on IR0_Data
  Register #(.Bits(4)) FLAG (.D(alu_1_p4), .C(C), .en(STORE_FLAG), .Q(FLAG_Data));
  // instruction_decoder instruction_decoder_1: pin names not known; wires that end beside it: ll, IR0_Data, ooo, instruction_decoder_1_p4, vvv, instruction_decoder_1_p6, imm8, rs0, rs1, imm16
  Register #(.Bits(8)) IR1 (.D(driver_1_out), .C(C), .en(IR1_RD), .Q(instruction_decoder_1_p4));
  Register #(.Bits(8)) IR2 (.D(driver_1_out), .C(C), .en(IR2_RD), .Q(instruction_decoder_1_p6));

  // Other names for the same wires on the sheet: MEM_ADDR[13:0] = ABUS[13:0]; MEM_SEL[1:0] = ABUS[15:14]; CLK = C

  // Notes on the sheet:
  //   C: Hz: 5
  //   RS Pair Decoder
  //   DBUS Read Decoder
  //   Branch Logic
  //   ALU Decoder
  //   Program Counter
  //   Microcode and Clock
  //   Stack Pointer
  //   DBUS Write Decoder
  //   DBUS Signals
  //   ABUS Decoder
  //   contents of rom_1 (hex, n*v repeats v):
  //   48,24,1,48,0,2,6e,0,73,28,48,0,4,1c,b,68,11,8b,40,0,9,50,1,1,6c
  //   ,2,6e,4,a,50,1,2,6e,e6,6e,fe,70,72,69,6e,74,66,20,72,75,6c,65
  //   ,73,21
  //   Bus Transceiver
  //   DBUS
  //   ABUS
  //   Registers
  //   ALU and FLAG
  //   IRs and Decoder
endmodule
