// Digital circuit microcode.dig as structural Verilog
module microcode (
  input  [7:0] d0,
  input  c,
  input  uPC_clr_2,
  output uPC_CLR,
  output PC_INC,
  output PCL_WE,
  output PCH_WE,
  output IR0_RD,
  output IR1_RD,
  output IR2_RD,
  output SP_INC,
  output SP_DEC,
  output [2:0] DB_RD_DEV,
  output [2:0] DB_WR_DEV,
  output [2:0] AB_WR_DEV,
  output STORE_FLAG,
  output STORE_ACC,
  output MEM_WE,
  output MEM_OE,
  output [2:0] PC_SRC,
  output uPC_Cond_CLR,
  output [3:0] uPC,
  output [11:0] ADDR,
  output STORE_N,
  output STORE_V,
  output STORE_C,
  output STORE_Z
);

  wire or_1_out;
  wire [5:4] _3_d;

  ROM #(.AddrBits(12), .Bits(8)) _3 (
    .A({d0, ADDR[3:0]}), .sel(1'b1), .D({MEM_OE, MEM_WE, _3_d, STORE_V, STORE_Z, STORE_N, STORE_C}));
  or or_1 (or_1_out, uPC_clr_2, uPC_CLR);
  ROM #(.AddrBits(12), .Bits(8)) _2 (
    .A({d0, ADDR[3:0]}), .sel(1'b1), .D({STORE_ACC, STORE_FLAG, DB_WR_DEV, DB_RD_DEV}));
  Counter #(.Bits(4)) u_uPC (.en(1'b1), .C(c), .clr(or_1_out), .out(ADDR[3:0]));  // open: ovf
  ROM #(.AddrBits(12), .Bits(8)) _1 (
    .A({d0, ADDR[3:0]}), .sel(1'b1), .D({AB_WR_DEV, SP_DEC, SP_INC, IR2_RD, IR1_RD, IR0_RD}));
  ROM #(.AddrBits(12), .Bits(8)) _0 (
    .A({d0, ADDR[3:0]}), .sel(1'b1), .D({PC_SRC, PCH_WE, PCL_WE, PC_INC, uPC_Cond_CLR, uPC_CLR}));

  assign ADDR[11:4] = d0;
  assign uPC = ADDR[3:0];

  // Notes on the sheet:
  //   contents of _3 (hex, n*v repeats v):
  //   80,15*0,80,15*0,80,15*0,80,15*0,80,15*0,80,15*0,80,15*0,80,15*0
  //   ,80,15*0,80,15*0,80,15*0,80,15*0,80,15*0,80,15*0,80,15*0,80,15*0
  //   ,80,15*0,80,15*0,80,15*0,80,15*0,80,15*0,80,15*0,80,15*0,80,15*0
  //   ,80,15*0,80,15*0,80,15*0,80,15*0,80,15*0,80,15*0,80,15*0,80,15*0
  //   ,80,15*0,80,15*0,80,15*0,80,15*0,80,15*0,80,15*0,80,15*0,80,15*0
  //   ,80,15*0,80,15*0,80,15*0,80,15*0,80,15*0,80,15*0,80,15*0,80,15*0
  //   ,80,15*0,80,15*0,80,15*0,80,15*0,80,15*0,80,15*0,80,15*0,80,15*0
  //   ,80,0,80,0,80,11*0,80,239*0,80,80,14*0,80,80,14*0,80,80,14*0,80,80
  //   ,14*0,80,80,14*0,80,80,14*0,80,80,14*0,80,80,14*0,80,80,14*0,80,80
  //   ,14*0,80,80,14*0,80,80,14*0,80,80,14*0,80,80,14*0,80,80,14*0,80,80
  //   ,14*0,80,0,80,13*0,80,0,80,13*0,80,0,80,13*0,80,0,80,13*0,80,0
  //   ,80,13*0,80,0,80,13*0,80,0,80,13*0,80,0,80,13*0,80,40,14*0,80
  //   ,40,14*0,80,40,14*0,80,40,14*0,80,40,14*0,80,40,14*0,80,40,14*0
  //   ,80,40,14*0,80,80,14*0,80,80,14*0,80,80,14*0,80,80,14*0,80,80
  //   ,14*0,80,80,14*0,80,80,14*0,80,80,14*0,80,80,80,13*0,80,80,80
  //   ,13*0,80,80,80,13*0,80,80,80,13*0,80,80,80,13*0,80,80,80,13*0
  //   ,80,80,80,13*0,80,80,80,13*0,80,80,40,13*0,80,80,40,13*0,80,80
  //   ,40,13*0,80,80,40,13*0,80,80,40,13*0,80,80,40,13*0,80,80,40,13*0
  //   ,80,80,40,13*0,4*80,12*0,4*80,12*0,4*80,12*0,4*80,12*0,4*80,12*0
  //   ,4*80,12*0,4*80,12*0,4*80,12*0,80,80,80,40,12*0,80,80,80,40,12*0
  //   ,80,80,80,40,12*0,80,80,80,40,12*0,80,80,80,40,12*0,80,80,80,40
  //   ,12*0,80,80,80,40,12*0,80,80,80,40,12*0,80,80,80,40,40,11*0,80,80,80
  //   ,40,40,11*0,80,80,80,40,40,11*0,80,80,80,40,40,11*0,80,80,80,40,40
  //   ,11*0,80,80,80,40,40,11*0,80,80,80,40,40,11*0,80,80,80,40,40,11*0
  //   ,80,80,80,13*0,80,80,80,13*0,80,80,80,13*0,80,80,80,13*0,80,80,80
  //   ,13*0,80,80,80,13*0,80,80,80,13*0,80,80,80
  //   contents of _2 (hex, n*v repeats v):
  //   38,61,14*0,38,61,14*0,38,61,14*0,38,61,14*0,38,61,14*0,38,61,14*0
  //   ,38,61,14*0,38,61,14*0,38,c0,14*0,38,c0,14*0,38,c0,14*0,38,c0
  //   ,14*0,38,c0,14*0,38,c0,14*0,38,c0,14*0,38,c0,14*0,38,c0,14*0,38
  //   ,c0,14*0,38,c0,14*0,38,c0,14*0,38,c0,14*0,38,c0,14*0,38,c0,14*0
  //   ,38,c0,14*0,38,c0,14*0,38,c0,14*0,38,c0,14*0,38,c0,14*0,38,c0
  //   ,14*0,38,c0,14*0,38,c0,14*0,38,c0,14*0,38,c0,14*0,38,c0,14*0,38
  //   ,c0,14*0,38,c0,14*0,38,c0,14*0,38,c0,14*0,38,c0,14*0,38,c0,14*0
  //   ,38,c0,14*0,38,c0,14*0,38,c0,14*0,38,c0,14*0,38,c0,14*0,38,c0
  //   ,14*0,38,c0,14*0,38,c0,14*0,38,c0,14*0,38,c0,14*0,38,c0,14*0,38
  //   ,c0,14*0,38,c0,14*0,38,c0,14*0,38,c0,14*0,38,c0,14*0,38,0,38,0
  //   ,38,11*0,38,239*0,38,38,c0,13*0,38,38,c0,13*0,38,38,c0,13*0,38,38
  //   ,c0,13*0,38,38,c0,13*0,38,38,c0,13*0,38,38,c0,13*0,38,38,c0,13*0
  //   ,38,38,c0,13*0,38,38,c0,13*0,38,38,c0,13*0,38,38,c0,13*0,38,38
  //   ,c0,13*0,38,38,c0,13*0,38,38,c0,13*0,38,38,c0,13*0,38,0,39,13*0
  //   ,38,0,39,13*0,38,0,39,13*0,38,0,39,13*0,38,0,39,13*0,38,0,39,13*0
  //   ,38,0,39,13*0,38,0,39,13*0,38,8,14*0,38,8,14*0,38,8,14*0,38,8
  //   ,14*0,38,8,14*0,38,8,14*0,38,8,14*0,38,8,14*0,38,38,14*0,38,38
  //   ,14*0,38,38,14*0,38,38,14*0,38,38,14*0,38,38,14*0,38,38,14*0,38,38
  //   ,14*0,38,38,39,13*0,38,38,39,13*0,38,38,39,13*0,38,38,39,13*0
  //   ,38,38,39,13*0,38,38,39,13*0,38,38,39,13*0,38,38,39,13*0,38,38
  //   ,8,13*0,38,38,8,13*0,38,38,8,13*0,38,38,8,13*0,38,38,8,13*0,38,38
  //   ,8,13*0,38,38,8,13*0,38,38,8,13*0,38,38,38,39,12*0,38,38,38,39
  //   ,12*0,38,38,38,39,12*0,38,38,38,39,12*0,38,38,38,39,12*0,38,38,38
  //   ,39,12*0,38,38,38,39,12*0,38,38,38,39,12*0,38,38,38,8,12*0,38,38,38
  //   ,8,12*0,38,38,38,8,12*0,38,38,38,8,12*0,38,38,38,8,12*0,38,38,38
  //   ,8,12*0,38,38,38,8,12*0,38,38,38,8,12*0,38,38,38,28,30,11*0,38,38,38
  //   ,28,30,11*0,38,38,38,28,30,11*0,38,38,38,28,30,11*0,38,38,38,28
  //   ,30,11*0,38,38,38,28,30,11*0,38,38,38,28,30,11*0,38,38,38,28,30
  //   ,11*0,38,38,38,13*0,38,38,38,13*0,38,38,38,13*0,38,38,38,13*0
  //   ,38,38,38,13*0,38,38,38,13*0,38,38,38,13*0,38,38,38
  //   contents of _1 (hex, n*v repeats v):
  //   21,15*0,21,15*0,21,15*0,21,15*0,21,15*0,21,15*0,21,15*0,21,15*0
  //   ,21,15*0,21,15*0,21,15*0,21,15*0,21,15*0,21,15*0,21,15*0,21,15*0
  //   ,21,15*0,21,15*0,21,15*0,21,15*0,21,15*0,21,15*0,21,15*0,21,15*0
  //   ,21,15*0,21,15*0,21,15*0,21,15*0,21,15*0,21,15*0,21,15*0,21,15*0
  //   ,21,15*0,21,15*0,21,15*0,21,15*0,21,15*0,21,15*0,21,15*0,21,15*0
  //   ,21,15*0,21,15*0,21,15*0,21,15*0,21,15*0,21,15*0,21,15*0,21,15*0
  //   ,21,15*0,21,15*0,21,15*0,21,15*0,21,15*0,21,15*0,21,15*0,21,15*0
  //   ,21,10,40,10,40,11*0,21,239*0,21,22,14*0,21,22,14*0,21,22,14*0
  //   ,21,22,14*0,21,22,14*0,21,22,14*0,21,22,14*0,21,22,14*0,21,22
  //   ,14*0,21,22,14*0,21,22,14*0,21,22,14*0,21,22,14*0,21,22,14*0,21
  //   ,22,14*0,21,22,14*0,21,10,40,13*0,21,10,40,13*0,21,10,40,13*0
  //   ,21,10,40,13*0,21,10,40,13*0,21,10,40,13*0,21,10,40,13*0,21,10
  //   ,40,13*0,21,48,14*0,21,48,14*0,21,48,14*0,21,48,14*0,21,48,14*0
  //   ,21,48,14*0,21,48,14*0,21,48,14*0,21,22,14*0,21,22,14*0,21,22
  //   ,14*0,21,22,14*0,21,22,14*0,21,22,14*0,21,22,14*0,21,22,14*0,21
  //   ,22,60,13*0,21,22,60,13*0,21,22,60,13*0,21,22,60,13*0,21,22,60
  //   ,13*0,21,22,60,13*0,21,22,60,13*0,21,22,60,13*0,21,22,60,13*0
  //   ,21,22,60,13*0,21,22,60,13*0,21,22,60,13*0,21,22,60,13*0,21,22
  //   ,60,13*0,21,22,60,13*0,21,22,60,13*0,21,22,24,80,12*0,21,22,24
  //   ,80,12*0,21,22,24,80,12*0,21,22,24,80,12*0,21,22,24,80,12*0,21
  //   ,22,24,80,12*0,21,22,24,80,12*0,21,22,24,80,12*0,21,22,24,80,12*0
  //   ,21,22,24,80,12*0,21,22,24,80,12*0,21,22,24,80,12*0,21,22,24,80
  //   ,12*0,21,22,24,80,12*0,21,22,24,80,12*0,21,22,24,80,12*0,21,22
  //   ,24,48,48,11*0,21,22,24,48,48,11*0,21,22,24,48,48,11*0,21,22,24
  //   ,48,48,11*0,21,22,24,48,48,11*0,21,22,24,48,48,11*0,21,22,24,48,48
  //   ,11*0,21,22,24,48,48,11*0,21,22,24,13*0,21,22,24,13*0,21,22,24
  //   ,13*0,21,22,24,13*0,21,22,24,13*0,21,22,24,13*0,21,22,24,13*0
  //   ,21,22,24
  //   contents of _0 (hex, n*v repeats v):
  //   4,1,14*0,4,1,14*0,4,1,14*0,4,1,14*0,4,1,14*0,4,1,14*0,4,1,14*0
  //   ,4,1,14*0,4,1,14*0,4,1,14*0,4,1,14*0,4,1,14*0,4,1,14*0,4,1,14*0
  //   ,4,1,14*0,4,1,14*0,4,1,14*0,4,1,14*0,4,1,14*0,4,1,14*0,4,1,14*0
  //   ,4,1,14*0,4,1,14*0,4,1,14*0,4,1,14*0,4,1,14*0,4,1,14*0,4,1,14*0
  //   ,4,1,14*0,4,1,14*0,4,1,14*0,4,1,14*0,4,1,14*0,4,1,14*0,4,1,14*0
  //   ,4,1,14*0,4,1,14*0,4,1,14*0,4,1,14*0,4,1,14*0,4,1,14*0,4,1,14*0
  //   ,4,1,14*0,4,1,14*0,4,1,14*0,4,1,14*0,4,1,14*0,4,1,14*0,4,1,14*0
  //   ,4,1,14*0,4,1,14*0,4,1,14*0,4,1,14*0,4,1,14*0,4,1,14*0,4,1,14*0
  //   ,4,0,10,0,9,11*0,4,239*0,4,4,1,13*0,4,4,1,13*0,4,4,1,13*0,4,4
  //   ,1,13*0,4,4,1,13*0,4,4,1,13*0,4,4,1,13*0,4,4,1,13*0,4,4,1,13*0
  //   ,4,4,1,13*0,4,4,1,13*0,4,4,1,13*0,4,4,1,13*0,4,4,1,13*0,4,4,1
  //   ,13*0,4,4,1,13*0,4,0,1,13*0,4,0,1,13*0,4,0,1,13*0,4,0,1,13*0,4
  //   ,0,1,13*0,4,0,1,13*0,4,0,1,13*0,4,0,1,13*0,4,1,14*0,4,1,14*0,4
  //   ,1,14*0,4,1,14*0,4,1,14*0,4,1,14*0,4,1,14*0,4,1,14*0,4,6,50,29
  //   ,12*0,4,6,50,29,12*0,4,6,50,29,12*0,4,6,50,29,12*0,4,6,50,29,12*0
  //   ,4,6,50,29,12*0,4,6,50,29,12*0,4,6,50,29,12*0,4,4,1,13*0,4,4,1
  //   ,13*0,4,4,1,13*0,4,4,1,13*0,4,4,1,13*0,4,4,1,13*0,4,4,1,13*0,4,4
  //   ,1,13*0,4,4,1,13*0,4,4,1,13*0,4,4,1,13*0,4,4,1,13*0,4,4,1,13*0
  //   ,4,4,1,13*0,4,4,1,13*0,4,4,1,13*0,4,4,4,1,12*0,4,4,4,1,12*0,4,4,4
  //   ,1,12*0,4,4,4,1,12*0,4,4,4,1,12*0,4,4,4,1,12*0,4,4,4,1,12*0,4,4,4
  //   ,1,12*0,4,4,4,1,12*0,4,4,4,1,12*0,4,4,4,1,12*0,4,4,4,1,12*0,4,4,4
  //   ,1,12*0,4,4,4,1,12*0,4,4,4,1,12*0,4,4,4,1,12*0,4,4,4,0,0,90,69
  //   ,9*0,4,4,4,0,0,90,69,9*0,4,4,4,0,0,90,69,9*0,4,4,4,0,0,90,69,9*0
  //   ,4,4,4,0,0,90,69,9*0,4,4,4,0,0,90,69,9*0,4,4,4,0,0,90,69,9*0,4,4,4
  //   ,0,0,90,69,9*0,4,6,4,90,69,11*0,4,6,4,90,69,11*0,4,6,4,90,69,11*0
  //   ,4,6,4,90,69,11*0,4,6,4,90,69,11*0,4,6,4,90,69,11*0,4,6,4,90,69
  //   ,11*0,4,6,4,90,69
endmodule
