// Digital circuit test.dig as structural Verilog
module test (
  input  [7:0] in_1,
  input  in_2,
  input  [7:0] in_3,
  input  in_4,
  input  [7:0] in_5,
  input  in_6,
  input  [7:0] in_7,
  input  in_8,
  input  in_9,
  input  in_10
);

  wire [7:0] driver_1_out, driver_2_out;

  assign driver_1_out = in_8 ? in_7 : 8'bz;  // Driver driver_1
  bus_transceiver bus_transceiver_1 (.dir(in_9), .oe(in_10), .a(driver_2_out), .b(driver_1_out));
  assign driver_2_out = in_2 ? in_1 : 8'bz;  // Driver driver_2
  assign driver_1_out = in_6 ? in_5 : 8'bz;  // Driver driver_3
  assign driver_2_out = in_4 ? in_3 : 8'bz;  // Driver driver_4
endmodule
