// Digital circuit write_dbus_signals.dig as structural Verilog
module write_dbus_signals (
  input  [2:0] vvv,
  input  [2:0] rs0,
  input  [2:0] rs1,
  input  R_vvv,
  input  R_rs0,
  input  R_rs1,
  output A,
  output B,
  output C,
  output D,
  output SP_Hi,
  output SP_Lo
);

  wire WR_RS0_MUX_1, WR_RS0_MUX_2, WR_RS0_MUX_3, WR_RS0_MUX_4, WR_RS0_MUX_5, WR_RS0_MUX_6, WR_RS0_MUX_7,
       WR_RS1_MUX_1, WR_RS1_MUX_2, WR_RS1_MUX_3, WR_RS1_MUX_4, WR_RS1_MUX_5, WR_RS1_MUX_6, WR_RS1_MUX_7,
       WR_VVV_MUX_1, WR_VVV_MUX_2, WR_VVV_MUX_3, WR_VVV_MUX_4, WR_VVV_MUX_5, WR_VVV_MUX_6, WR_VVV_MUX_7;

  or or_1 (SP_Hi, WR_RS0_MUX_7, WR_RS1_MUX_7, WR_VVV_MUX_7);
  or or_2 (SP_Lo, WR_RS0_MUX_6, WR_RS1_MUX_6, WR_VVV_MUX_6);
  or or_3 (D, WR_RS0_MUX_4, WR_RS1_MUX_4, WR_VVV_MUX_4);
  or or_4 (C, WR_RS0_MUX_3, WR_RS1_MUX_3, WR_VVV_MUX_3);
  Demultiplexer #(.Selector_Bits(3)) demultiplexer_1 (
    .sel(rs1), .in(R_rs1), .out_1(WR_RS1_MUX_1), .out_2(WR_RS1_MUX_2), .out_3(WR_RS1_MUX_3),
    .out_4(WR_RS1_MUX_4), .out_5(WR_RS1_MUX_5), .out_6(WR_RS1_MUX_6), .out_7(WR_RS1_MUX_7));  // open: out_0
  or or_5 (B, WR_RS0_MUX_2, WR_RS1_MUX_2, WR_VVV_MUX_2);
  or or_6 (A, WR_RS0_MUX_1, WR_RS1_MUX_1, WR_VVV_MUX_1);
  Demultiplexer #(.Selector_Bits(3)) demultiplexer_2 (
    .sel(vvv), .in(R_vvv), .out_1(WR_VVV_MUX_1), .out_2(WR_VVV_MUX_2), .out_3(WR_VVV_MUX_3),
    .out_4(WR_VVV_MUX_4), .out_5(WR_VVV_MUX_5), .out_6(WR_VVV_MUX_6), .out_7(WR_VVV_MUX_7));  // open: out_0
  Demultiplexer #(.Selector_Bits(3)) demultiplexer_3 (
    .sel(rs0), .in(R_rs0), .out_1(WR_RS0_MUX_1), .out_2(WR_RS0_MUX_2), .out_3(WR_RS0_MUX_3),
    .out_4(WR_RS0_MUX_4), .out_5(WR_RS0_MUX_5), .out_6(WR_RS0_MUX_6), .out_7(WR_RS0_MUX_7));  // open: out_0

  // Other names for the same wires on the sheet: WR_R_rs0 = R_rs0; WR_R_rs1 = R_rs1; WR_R_vvvv = R_vvv
endmodule
